# Fritzing sketch sketch (saved by Fritzing 0.9.9b)
circuit board: 8cm x 9cm
breadboards: 2

parts:
  part = LuaNode32 / ESP32 [part_number=ESP32S-PIN30]
  RY1 = SSR-40VA
  part_2 = female pin header, 2 pins [form="♀ (female)"]

nets:
  N1: part.D13, RY1.Pin_3, part_2.pin2
  N2: part.GND, RY1.Pin_4, part_2.pin1

notes:
  github.com/
  jsfraz/daylight
  SSR relay

custom parts:
  LuaNode32 / ESP32: New Image for LuaNode32 DOIT ESP32 DEVKIT V1. Base parts from LuaNode32 / ESP32 ESP32 based LuaNode32 by G.Noorlander DOIT Esp32 DevKit v1 (30 pins long, 11 pins width) by Werner Rothschopf (modified by vanepp Dec 2018)
  SSR-40VA: SSR-40VA solid state relay.
